// Logisim project RSC.circ as structural Verilog: 9 circuits, main circuit Logic_U
// LU
module Logic_U (
  input  [31:0] A,
  input  [31:0] B,
  input  S1,
  input  S2,
  output [31:0] Logic_out
);

  wire [31:0] and_1_out, not_1_out, or_1_out, shifter_1_out;

  assign and_1_out = A & B;  // AND_Gate and_1, 32 bits wide
  assign or_1_out = A | B;  // OR_Gate or_1, 32 bits wide
  Shifter #(.width(32), .shift("ar")) shifter_1 (.in(A), .\dist (5'b00001), .out(shifter_1_out));
  assign not_1_out = ~A;  // NOT_Gate not_1, 32 bits wide
  Multiplexer #(.select(2), .width(32), .enable("false")) multiplexer_1 (
    .in0(and_1_out), .in1(or_1_out), .in2(shifter_1_out), .in3(not_1_out), .out(Logic_out), .sel({S1, S2}));

  // Notes on the sheet:
  //   Aaron Itzkovitz
  //   CLA6
  //   Logic Unit
endmodule

module ALU (
  input  [31:0] A,
  input  [31:0] B,
  input  S2,
  input  S1,
  input  S0,
  output [31:0] ALO_Out
);

  wire [31:0] arith_u_1_au_out, logic_u_1_logic_out;

  Arith_U arith_u_1 (.A(A), .B(B), .S1(S1), .S0(S0), .AU_out(arith_u_1_au_out));  // open: Cout
  Multiplexer #(.width(32), .enable("false")) multiplexer_1 (
    .in0(arith_u_1_au_out), .in1(logic_u_1_logic_out), .out(ALO_Out), .sel(S2));
  Logic_U logic_u_1 (.A(A), .B(B), .S1(S1), .S2(S0), .Logic_out(logic_u_1_logic_out));

  // Notes on the sheet:
  //   Aaron Itzkovitz
  //   CLA6
  //   Arithmetic Logic Unit
endmodule

// AU
module Arith_U (
  input  [31:0] A,
  input  [31:0] B,
  input  S1,
  input  S0,
  output [31:0] AU_out,
  output Cout
);

  wire and_1_out, not_2_out;
  wire [31:0] multiplexer_1_out, multiplexer_2_out, nor_1_out, not_1_out;

  assign not_1_out = ~B;  // NOT_Gate not_1, 32 bits wide
  assign nor_1_out = ~(A | {32{1'b1}});  // NOR_Gate nor_1, 32 bits wide
  Multiplexer #(.select(2), .width(32), .enable("false")) multiplexer_1 (
    .in0(not_1_out), .in1(B), .in2(nor_1_out), .in3(B), .out(multiplexer_1_out), .sel({S1, S0}));
  Multiplexer #(.width(32), .enable("false")) multiplexer_2 (
    .in0(A), .in1({32{1'b0}}), .out(multiplexer_2_out), .sel(and_1_out));
  not not_2 (not_2_out, S0);
  and and_1 (and_1_out, S0, S1);
  Adder #(.width(32)) adder_1 (
    .a(multiplexer_2_out), .b(multiplexer_1_out), .out(AU_out), .cin(not_2_out), .cout(Cout));

  // Notes on the sheet:
  //   Aaron Itzkovitz
  //   CLA 4
  //   Arithmetic Unit
endmodule

module SC (
  input  Clock,
  input  Clear,
  output [2:0] SEQ_out
);

  wire [2:0] adder_1_out;

  Adder #(.width(3)) adder_1 (.a(SEQ_out), .b(3'b001), .out(adder_1_out), .cin(1'b0));  // open: cout
  Register #(.width(3)) register_1 (.D(adder_1_out), .en(1'b1), .Q(SEQ_out), .clk(Clock), .clr(Clear));

  // Notes on the sheet:
  //   Aaron Itzkovitz
  //   CLA 7
  //   Sequence Counter Circuit
endmodule

// DEC
module Decoder (
  input  [31:0] IR_In,
  output [15:0] D_Out,
  output [3:0] Debug_Instruction
);

  wire or_1_out;
  wire [3:0] or_2_out;
  wire [15:0] decoder_1_out0;

  Multiplexer #(.width(16), .enable("false")) multiplexer_1 (
    .in0(decoder_1_out0), .in1({16{1'b0}}), .out(D_Out), .sel(or_1_out));
  or or_1 (or_1_out, or_2_out[0], or_2_out[1], or_2_out[2], or_2_out[3]);
  assign or_2_out = IR_In[7:4] | IR_In[11:8] | IR_In[15:12] | IR_In[19:16] | IR_In[23:20] | IR_In[27:24] | IR_In[31:28];  // OR_Gate or_2, 4 bits wide
  Decoder_part #(.select(4), .enable("false")) decoder_1 (
    .out0(decoder_1_out0[0]), .out1(decoder_1_out0[1]), .out2(decoder_1_out0[2]), .out3(decoder_1_out0[3]),
    .out4(decoder_1_out0[4]), .out5(decoder_1_out0[5]), .out6(decoder_1_out0[6]), .out7(decoder_1_out0[7]),
    .out8(decoder_1_out0[8]), .out9(decoder_1_out0[9]), .out10(decoder_1_out0[10]),
    .out11(decoder_1_out0[11]), .out12(decoder_1_out0[12]), .out13(decoder_1_out0[13]),
    .out14(decoder_1_out0[14]), .out15(decoder_1_out0[15]), .sel(IR_In[3:0]));

  assign Debug_Instruction = IR_In[3:0];

  // Notes on the sheet:
  //   Aaron Itzkovitz
  //   CLA8
  //   Decoder Circuit
endmodule

// TIME
module Timer (
  input  Clock,
  input  Stop,
  input  Clear,
  output [7:0] T_Out
);

  wire [2:0] sc_1_seq_out;
  wire [7:0] decoder_1_out0;

  Multiplexer #(.width(8), .enable("false")) multiplexer_1 (
    .in0(decoder_1_out0), .in1({8{1'b0}}), .out(T_Out), .sel(Stop));
  Decoder_part #(.select(3), .enable("false")) decoder_1 (
    .out0(decoder_1_out0[0]), .out1(decoder_1_out0[1]), .out2(decoder_1_out0[2]), .out3(decoder_1_out0[3]),
    .out4(decoder_1_out0[4]), .out5(decoder_1_out0[5]), .out6(decoder_1_out0[6]), .out7(decoder_1_out0[7]),
    .sel(sc_1_seq_out));
  SC sc_1 (.Clear(Clear), .Clock(Clock), .SEQ_out(sc_1_seq_out));

  // Notes on the sheet:
  //   Aaron Itzkovitz
  //   CLA8
  //   Timer Circuit
endmodule

module RSC (
  output [31:0] out_1,
  output [31:0] D,
  output [7:0] T,
  output [3:0] D_2,
  output [31:0] D_3,
  output [31:0] D_4
);

  wire acc_1_p2, acc_1_p4, acc_1_p5, ar_1_p3, control_1_ram_en, control_1_ram_r_prime_w, control_1_z_ld,
       dr_1_p3, dr_1_p4, ir_1_p3, outr_1_p3, pc_1_p2, pc_1_p4, pc_1_p5, Primary_Clock_out, r_1_p3, r_1_p4,
       z_reg_1_z_out;
  wire [2:0] control_1_alu_s;
  wire [31:0] alu_1_alo_out, ar_1_p4, ir_1_p4;

  Clock Primary_Clock (.out(Primary_Clock_out));
  Hex_Digit_Display hex_digit_display_1 (.value(D_3[31:28]), .dp(1'b0));
  // AR ar_1: pin names not known; wires that end beside it: out_1, Primary_Clock_out, ar_1_p3, ar_1_p4, ar_1_p4
  // R r_1: pin names not known; wires that end beside it: out_1, Primary_Clock_out, r_1_p3, r_1_p4, out_1
  // OUTR outr_1: pin names not known; wires that end beside it: out_1, Primary_Clock_out, outr_1_p3, D_3
  Hex_Digit_Display hex_digit_display_2 (.value(D_3[27:24]), .dp(1'b0));
  // DR dr_1: pin names not known; wires that end beside it: out_1, Primary_Clock_out, dr_1_p3, dr_1_p4, D, out_1
  ALU alu_1 (
    .A(D_4), .B(out_1), .S2(control_1_alu_s[2]), .S1(control_1_alu_s[1]), .S0(control_1_alu_s[0]),
    .ALO_Out(alu_1_alo_out));
  Hex_Digit_Display hex_digit_display_3 (.value(D_3[23:20]), .dp(1'b0));
  Hex_Digit_Display hex_digit_display_4 (.value(D_3[19:16]), .dp(1'b0));
  RAM #(.addrWidth(16), .dataWidth(32)) ram_1 (
    .addr(ar_1_p4[15:0]), .data(out_1), .sel(control_1_ram_en), .clk(Primary_Clock_out),
    .ld(control_1_ram_r_prime_w), .clr(1'b0));
  // PC pc_1: pin names not known; wires that end beside it: out_1, pc_1_p2, Primary_Clock_out, pc_1_p4, pc_1_p5, out_1
  // ACC acc_1: pin names not known; wires that end beside it: alu_1_alo_out, acc_1_p2, Primary_Clock_out, acc_1_p4, acc_1_p5, D_4, out_1
  Hex_Digit_Display hex_digit_display_5 (.value(D_3[15:12]), .dp(1'b0));
  Z_Reg z_reg_1 (.ACC_In(D_4), .Clock(Primary_Clock_out), .Load(control_1_z_ld), .Z_Out(z_reg_1_z_out));
  Hex_Digit_Display hex_digit_display_6 (.value(D_3[7:4]), .dp(1'b0));
  Hex_Digit_Display hex_digit_display_7 (.value(D_3[11:8]), .dp(1'b0));
  // IR ir_1: pin names not known; wires that end beside it: D, Primary_Clock_out, ir_1_p3, ir_1_p4
  Control control_1 (
    .RAM_R_prime_W(control_1_ram_r_prime_w), .RAM_EN(control_1_ram_en), .AR_LD(ar_1_p3), .PC_BUS(pc_1_p5),
    .PC_INC(pc_1_p2), .PC_LD(pc_1_p4), .DR_BUS(dr_1_p4), .DR_LD(dr_1_p3), .R_BUS(r_1_p4), .R_LD(r_1_p3),
    .ACC_BUS(acc_1_p5), .ACC_CLR(acc_1_p4), .ACC_LD(acc_1_p2), .ALU_S(control_1_alu_s), .OUTR_LD(outr_1_p3),
    .Z_LD(control_1_z_ld), .IR_LD(ir_1_p3), .Clock(Primary_Clock_out), .Z_In(z_reg_1_z_out), .T(T),
    .IR_In(ir_1_p4), .D(D_2));
  Hex_Digit_Display hex_digit_display_8 (.value(D_3[3:0]), .dp(1'b0));

  // Notes on the sheet:
  //   Aaron Itzkovitz
  //   RSC Outline
  //   OLA6
endmodule

// Z
module Z_Reg (
  input  Clock,
  input  [31:0] ACC_In,
  input  Load,
  output Z_Out
);

  wire not_1_out, or_2_out;
  wire [3:0] or_1_out;

  assign or_1_out = ACC_In[3:0] | ACC_In[7:4] | ACC_In[11:8] | ACC_In[15:12] | ACC_In[19:16] | ACC_In[23:20] | ACC_In[27:24] | ACC_In[31:28];  // OR_Gate or_1, 4 bits wide
  or or_2 (or_2_out, or_1_out[0], or_1_out[1], or_1_out[2], or_1_out[3]);
  not not_1 (not_1_out, or_2_out);
  // _1bit_reg 1bit_reg_1: pin names not known; wires that end beside it: not_1_out, Clock, Load, 1'b0, Z_Out
endmodule

module Control (
  input  Clock,
  input  [31:0] IR_In,
  input  Z_In,
  output IR_LD,
  output [7:0] T,
  output RAM_R_prime_W,
  output RAM_EN,
  output AR_LD,
  output PC_BUS,
  output [3:0] D,
  output PC_INC,
  output PC_LD,
  output DR_BUS,
  output DR_LD,
  output R_BUS,
  output R_LD,
  output ACC_BUS,
  output ACC_CLR,
  output ACC_LD,
  output [2:0] ALU_S,
  output OUTR_LD,
  output Z_LD
);

  wire s_ld_1_p8, S_p5, sc_clr_1_p9;
  wire [15:0] ir_ld_1_p12;

  // IR_LD ir_ld_1: pin names not known; wires that end beside it: IR_LD, Clock, T[2], T[0], T[1], T[2], T[3], T[4], T[5], T[6], T[7], ir_ld_1_p12[0], ir_ld_1_p12[1]
  // RAM_RW ram_rw_1: pin names not known; wires that end beside it: RAM_R_prime_W, Z_In, ir_ld_1_p12[6], ir_ld_1_p12[5], ir_ld_1_p12[2], ir_ld_1_p12[1], T[5], T[3], T[1]
  // RAM_EN ram_en_1: pin names not known; wires that end beside it: RAM_EN, Z_In, ir_ld_1_p12[6], ir_ld_1_p12[5], ir_ld_1_p12[2], ir_ld_1_p12[1], T[6], T[5], T[3], T[1]
  // AR_LD ar_ld_1: pin names not known; wires that end beside it: AR_LD, ir_ld_1_p12[2], ir_ld_1_p12[1], Clock, T[4], T[2], T[0]
  // PC_BUS pc_bus_1: pin names not known; wires that end beside it: PC_BUS, T[2], T[0]
  // PC_INC pc_inc_1: pin names not known; wires that end beside it: PC_INC, Z_In, ir_ld_1_p12[6], ir_ld_1_p12[2], ir_ld_1_p12[1], Clock, T[3], T[1]
  // PC_LD pc_ld_1: pin names not known; wires that end beside it: PC_LD, Z_In, ir_ld_1_p12[6], ir_ld_1_p12[5], Clock, T[4]
  // DR_BUS dr_bus_1: pin names not known; wires that end beside it: DR_BUS, Z_In, ir_ld_1_p12[6], ir_ld_1_p12[5], ir_ld_1_p12[2], ir_ld_1_p12[1], T[6], T[4]
  // DR_LD dr_ld_1: pin names not known; wires that end beside it: DR_LD, Z_In, ir_ld_1_p12[6], ir_ld_1_p12[5], ir_ld_1_p12[2], ir_ld_1_p12[1], Clock, T[5], T[3], T[1]
  // R_BUS r_bus_1: pin names not known; wires that end beside it: R_BUS, ir_ld_1_p12[13], ir_ld_1_p12[12], ir_ld_1_p12[9], ir_ld_1_p12[8], ir_ld_1_p12[4], T[3]
  // R_LD r_ld_1: pin names not known; wires that end beside it: R_LD, Clock, ir_ld_1_p12[3], T[3]
  // ACC_BUS acc_bus_1: pin names not known; wires that end beside it: ACC_BUS, ir_ld_1_p12[7], ir_ld_1_p12[3], ir_ld_1_p12[2], T[5], T[3]
  // ACC_CLR acc_clr_1: pin names not known; wires that end beside it: ACC_CLR, ir_ld_1_p12[11], T[3], ir_ld_1_p12[15]
  // ACC_LD acc_ld_1: pin names not known; wires that end beside it: ACC_LD, ir_ld_1_p12[14], ir_ld_1_p12[13], ir_ld_1_p12[12], ir_ld_1_p12[10], ir_ld_1_p12[9], ir_ld_1_p12[8], ir_ld_1_p12[4], ir_ld_1_p12[1], Clock, T[6]
  // ALU_SEL alu_sel_1: pin names not known; wires that end beside it: T[3], ALU_S[2], ALU_S[1], ALU_S[0], ir_ld_1_p12[15], ir_ld_1_p12[14], ir_ld_1_p12[13], ir_ld_1_p12[12], ir_ld_1_p12[10], ir_ld_1_p12[9], ir_ld_1_p12[4], ir_ld_1_p12[1]
  // OUTR_LD outr_ld_1: pin names not known; wires that end beside it: OUTR_LD, ir_ld_1_p12[7], Clock, T[3]
  // Z_LD z_ld_1: pin names not known; wires that end beside it: Z_LD, T[0], T[1], T[2], T[3], T[4], T[5], T[6], T[7], Clock, ir_ld_1_p12[0], ir_ld_1_p12[1]
  // S_LD s_ld_1: pin names not known; wires that end beside it: ir_ld_1_p12[13], ir_ld_1_p12[14], ir_ld_1_p12[15], Z_In, T[3], ir_ld_1_p12[0], Clock, s_ld_1_p8
  // SC_CLR sc_clr_1: pin names not known; wires that end beside it: T[4], T[5], T[7], ir_ld_1_p12[1], ir_ld_1_p12[2], ir_ld_1_p12[5], ir_ld_1_p12[6], Z_In, sc_clr_1_p9
  Timer timer_1 (.T_Out(T), .Clock(Clock), .Stop(S_p5), .Clear(sc_clr_1_p9));
  // _1bit_reg S: pin names not known; wires that end beside it: 1'b1, Clock, s_ld_1_p8, 1'b1, S_p5
  Decoder decoder_1 (.D_Out(ir_ld_1_p12), .Debug_Instruction(D), .IR_In(IR_In));
endmodule
